# Fritzing sketch battery-toolbox (saved by Fritzing 1.0.1rc)
breadboards: 1

parts:
  U1 = LCD-16X2 [package=lcd-16x2_noholes]
  R3 = Resistor [tolerance=±5% power=0.25 resistance=220 package=THT]
  R4 = Trimmer Potentiometer [maximum_resistance=25kΩ knob_status=50% package=THT]
  U4_(Rotary_encoder) = ENCODER-QUADRATURE [package=encoder-16mm-quad]
  C3 = Ceramic Capacitor [capacitance=100nF voltage=35V package="100 mil [THT, multilayer]"]
  C4 = Ceramic Capacitor [capacitance=100nF voltage=35V package="100 mil [THT, multilayer]"]
  S1_(Rotary_Push)1 = Pushbutton [package="[THT]"]
  C5 = Ceramic Capacitor [capacitance=100nF voltage=35V package="100 mil [THT, multilayer]"]
  R8 = Resistor [tolerance=±5% power=0.25 resistance=50k package=THT]
  R9 = Resistor [tolerance=±5% power=0.25 resistance=22 package=THT]
  D2 = Zener Diode [breakdown_voltage=4.7V part_number=1N4732A package="Melf DO-213 AB [SMD]"]
  Part2 = Arduino Uno (Rev3)
  U5 = ACS712 [package=so08]
  Q1 = Basic FET N-Channel [part_number=D472 package="D2Pak [SMD]"]
  Fuse1 = Fuse with Handler [part_number=Htc-15A]
  C6 = Ceramic Capacitor [capacitance=1nF voltage=35V package="100 mil [THT, multilayer]"]
  R10 = Resistor [tolerance=±5% power=0.25 resistance=1.8k package=THT]
  R11 = Resistor [tolerance=±5% power=0.25 resistance=47k package=THT]
  C7 = Ceramic Capacitor [capacitance=100nF voltage=35V package="100 mil [THT, multilayer]"]
  C8 = Ceramic Capacitor [capacitance=100nF voltage=35V package="100 mil [THT, multilayer]"]
  R13 = Resistor [tolerance=±1% power=0.25W resistance=13k package=THT]
  R14 = Resistor [tolerance=±1% power=0.25 resistance=44.2k package=THT]
  C11 = Electrolytic Capacitor [capacitance=10µF voltage=6.3V package="100 mil [THT, electrolytic]"]
  R16 = Temperature Sensor (Thermistor) [thermistor_type=NTC part_number="B3950 (100K)" package=THT]
  R17 = Resistor [tolerance=±5% power=0.25 resistance=4.7k package=THT]
  C13 = Electrolytic Capacitor [capacitance=1mF voltage=6.3V package="100 mil [THT, electrolytic]"]
  R18 = Resistor [tolerance=±5% power=0.25 resistance=1k package=THT]
  J1 = Piezo Speaker
  R19 = Resistor [tolerance=±5% power=0.25 resistance=1.8k package=THT]
  R20 = Resistor [tolerance=±1% power=0.25W resistance=13k package=THT]
  R22 = Resistor [tolerance=±1% power=0.25 resistance=44.2k package=THT]
  U10 = RELAY [part_number=15A package=relay-t9a-2]
  Q6 = NPN-Transistor [package="TO92 [THT]"]
  D5 = Rectifier Diode [part_number=1N4001 package="300 mil [THT]"]
  U11 = Optocoupler [package=THT]
  LED3 = LED - 5mm [color="Red (633nm)" current=0.030 package="5 mm [THT]"]
  R27 = Resistor [tolerance=±5% power=0.25 resistance=510 package=THT]
  R28 = Resistor [tolerance=±5% power=0.25 resistance=1k package=THT]
  U12 = RELAY [part_number=15A package=relay-t9a-2]
  Q7 = NPN-Transistor [package="TO92 [THT]"]
  D6 = Rectifier Diode [part_number=1N4001 package="300 mil [THT]"]
  U13 = Optocoupler [package=THT]
  LED4 = LED - 5mm [color="Red (633nm)" current=0.030 package="5 mm [THT]"]
  R29 = Resistor [tolerance=±5% power=0.25 resistance=510 package=THT]
  R30 = Resistor [tolerance=±5% power=0.25 resistance=1k package=THT]
  Q8 = Basic FET N-Channel [part_number=D472 package="D2Pak [SMD]"]
  R31 = Resistor [tolerance=±5% power=0.25 resistance=1k package=THT]

nets:
  VSS: U1.VSS, U1.R_W, R4.leg2, Part2.GND, R17.Pin_0, J1.pin1
  5V: U1.VDD, U1.K, R3.Pin_1, R4.leg1, R8.Pin_1, R9.Pin_1, Part2.5V, U5.VCC, C8.1, C13.+, U10.COIL1, D5.cathode, U11.Pin_5, R28.Pin_0, U12.COIL1, D6.cathode, U13.Pin_5, R30.Pin_0
  N1: U1.VO, R4.wiper
  N2: U1.RS, Part2.D13/SCK
  N3: U1.E, Part2.D12/MISO
  N4: U1.DB4, Part2.D8
  N5: U1.DB5, Part2.D7
  N6: U1.DB6, Part2.D5_PWM
  N7: U1.DB7, Part2.D4
  N8: U1.A, R3.Pin_0
  N9: U4_(Rotary_encoder).A, C3.1, Part2.D2
  N10: U4_(Rotary_encoder).B, C4.1, Part2.D3_PWM
  Charging Supply (GND)/GND: U4_(Rotary_encoder).C, C3.0, C4.0, S1_(Rotary_Push)1.Pin_3, S1_(Rotary_Push)1.Pin_4, C5.0, D2.anode, U5.GND, Q1.source, C6.0, R11.Pin_0, C7.0, C8.0, R13.Pin_1, C11.-, C13.-, R20.Pin_1, U10.NO, Q6.E, Q7.E, Q8.source
  N11: S1_(Rotary_Push)1.Pin_1, S1_(Rotary_Push)1.Pin_2, C5.1, R8.Pin_0, Part2.A4/SDA
  N12: R9.Pin_0, D2.cathode, Part2.AREF, C11.+, R16.pin_1
  N13: Part2.A0, R13.Pin_0, R14.Pin_1
  N14: Part2.A1, R10.Pin_1, R11.Pin_1, C7.1
  N15: Part2.A2, R16.pin_0, R17.Pin_1
  N16: Part2.A5/SCL, R20.Pin_0, R22.Pin_1
  N17: Part2.D9_PWM, R18.Pin_1
  N18: Part2.D10_PWM/SS, R31.Pin_1
  N19: Part2.D11_PWM/MOSI, LED3.cathode, LED4.cathode
  N20: Part2.D6_PWM, R19.Pin_0
  +12V: Part2.VIN
  N21: U5.IP+, Fuse1.Connector1, R14.Pin_0
  N22: U5.IP-, Q1.drain, Q8.drain
  N23: U5.FILT, C6.1
  N24: U5.VOUT, R10.Pin_0
  N25: Q1.Gate, R18.Pin_0
  Discharging (Load-): Fuse1.Connector2, U10.NC
  N26: J1.pin2, R19.Pin_1
  BAT (+): R22.Pin_0, U12.MAIN
  N27: U10.COIL2, Q6.C, D5.anode
  BAT (-): U10.MAIN
  N28: Q6.B, R27.Pin_0
  N29: U11.Pin_1, R28.Pin_1
  N30: U11.Pin_2, LED3.anode
  N31: U11.Pin_4, R27.Pin_1
  N32: U12.COIL2, Q7.C, D6.anode
  Charging Supply (VDD): U12.NC
  Discharging (Load+): U12.NO
  N33: Q7.B, R29.Pin_0
  N34: U13.Pin_1, R30.Pin_1
  N35: U13.Pin_2, LED4.anode
  N36: U13.Pin_4, R29.Pin_1
  N37: Q8.Gate, R31.Pin_0
